# Fritzing sketch focuser (saved by Fritzing 0.9.0b)
circuit board: 7.39757cm x 3.17134cm
breadboards: 1

parts:
  J1 = male pin header, 14 pins [form="♂ (male)"]
  J2 = male pin header, 14 pins [form="♂ (male)"]
  J3 = male pin header, 8 pins [form="♂ (male)"]
  J4 = male pin header, 8 pins [form="♂ (male)"]
  J5 = male pin header, 4 pins [form="♂ (male)"]
  J6 = Screw terminal - 2 pins [package=THT]
  J7 = male pin header, 1 pin [form="♂ (male)"]
  J8 = male pin header, 2 pins [form="♂ (male)"]  # not connected

nets:
  N1: J1.pin1, J4.pin2
  N2: J2.pin1, J4.pin1
  N3: J2.pin10, J3.pin1
  N4: J2.pin11, J3.pin2
  N5: J3.pin3, J3.pin4
  N6: J3.pin8, J7.pin1
  N7: J4.pin3, J5.pin1
  N8: J4.pin4, J5.pin2
  N9: J4.pin5, J5.pin3
  N10: J4.pin6, J5.pin4
  N11: J4.pin7, J6.pin2
  N12: J4.pin8, J6.pin1
